// Logisim project PROJET AUTOMATISME.circ as structural Verilog: 13 circuits, main circuit ADDITIONNEUR 1 BIT
module ADDITIONNEUR_1_BIT (
  input  A,
  input  B,
  input  RE,
  output RS,
  output S
);

  wire and_1_out, and_2_out, and_3_out, and_4_out, not_1_out, not_2_out, or_1_out, xor_1_out, xor_2_out;

  not not_1 (not_1_out, B);
  not not_2 (not_2_out, RE);
  or or_1 (or_1_out, A, B);
  and and_1 (and_1_out, A, B);
  xor xor_1 (xor_1_out, A, B);
  xor xor_2 (xor_2_out, A, not_1_out);
  and and_2 (and_2_out, or_1_out, RE);
  and and_3 (and_3_out, xor_1_out, not_2_out);
  and and_4 (and_4_out, xor_2_out, RE);
  or or_2 (RS, and_2_out, and_1_out);
  or or_3 (S, and_3_out, and_4_out);
endmodule

module ADDITTIONNEUR_4_BIT (
  input  [3:0] in_1,
  input  [3:0] in_2,
  output [3:0] out_3,
  output out_4
);

  wire additionneur_1_bit_1_rs, additionneur_1_bit_2_rs, additionneur_1_bit_3_rs;

  ADDITIONNEUR_1_BIT additionneur_1_bit_1 (
    .A(in_1[0]), .B(in_2[0]), .RE(1'b0), .RS(additionneur_1_bit_1_rs), .S(out_3[0]));
  ADDITIONNEUR_1_BIT additionneur_1_bit_2 (
    .A(in_1[1]), .B(in_2[1]), .RE(additionneur_1_bit_1_rs), .RS(additionneur_1_bit_2_rs), .S(out_3[1]));
  ADDITIONNEUR_1_BIT additionneur_1_bit_3 (
    .A(in_1[2]), .B(in_2[2]), .RE(additionneur_1_bit_2_rs), .RS(additionneur_1_bit_3_rs), .S(out_3[2]));
  ADDITIONNEUR_1_BIT additionneur_1_bit_4 (
    .A(in_1[3]), .B(in_2[3]), .RE(additionneur_1_bit_3_rs), .RS(out_4), .S(out_3[3]));
endmodule

module MULTIPLEXER (
  input  SEL_0,
  input  SEL1,
  input  A,
  input  B,
  input  C,
  input  D,
  output S
);

  wire and_1_out, and_2_out, and_3_out, and_4_out, not_1_out, not_2_out;

  not not_1 (not_1_out, SEL_0);
  not not_2 (not_2_out, SEL1);
  and and_1 (and_1_out, not_1_out, not_2_out, A);
  and and_2 (and_2_out, not_1_out, SEL1, B);
  and and_3 (and_3_out, SEL_0, not_2_out, C);
  and and_4 (and_4_out, SEL_0, SEL1, D);
  or or_1 (S, and_1_out, and_2_out, and_3_out, and_4_out);
endmodule

module ALU (
  input  A,
  input  B,
  input  [2:0] in_3,
  input  in_4,
  output S,
  output RS
);

  wire additionneur_1_bit_1_s, and_1_out, not_1_out, or_1_out;

  or or_1 (or_1_out, A, B);
  and and_1 (and_1_out, B, B);
  not not_1 (not_1_out, B);
  ADDITIONNEUR_1_BIT additionneur_1_bit_1 (.A(A), .B(B), .RE(in_4), .RS(RS), .S(additionneur_1_bit_1_s));
  Multiplexer #(.select(3)) multiplexer_1 (
    .in0(or_1_out), .in1(and_1_out), .in2(not_1_out), .in3(additionneur_1_bit_1_s), .out(S), .sel(in_3));  // open: in4, in5, in6, in7, en
endmodule

module ALU_4__BIT (
  input  [3:0] in_1,
  input  [3:0] in_2,
  input  [2:0] in_3,
  output out_4,
  output [3:0] out_5
);

  wire alu_1_rs, alu_2_rs, alu_3_rs;

  ALU alu_1 (.A(in_1[0]), .B(in_2[0]), .in_4(1'b0), .S(out_5[3]), .RS(alu_1_rs), .in_3(in_3));
  ALU alu_2 (.A(in_1[1]), .B(in_2[1]), .in_4(alu_1_rs), .S(out_5[2]), .RS(alu_2_rs), .in_3(in_3));
  ALU alu_3 (.A(in_1[2]), .B(in_2[2]), .in_4(alu_2_rs), .S(out_5[1]), .RS(alu_3_rs), .in_3(in_3));
  ALU alu_4 (.A(in_1[3]), .B(in_2[3]), .in_4(alu_3_rs), .S(out_5[0]), .RS(out_4), .in_3(in_3));
endmodule

module DECODEUR (
  input  A,
  input  B,
  input  C,
  output S0,
  output S1,
  output S2,
  output S3,
  output S4,
  output S5,
  output S6,
  output S7
);

  wire not_1_out, not_2_out, not_3_out;

  not not_1 (not_1_out, A);
  not not_2 (not_2_out, B);
  not not_3 (not_3_out, C);
  and and_1 (S0, not_1_out, not_2_out, not_3_out);
  and and_2 (S1, A, B, not_3_out);
  and and_3 (S2, B, not_1_out, not_3_out);
  and and_4 (S3, not_1_out, B, C);
  and and_5 (S4, A, not_2_out, not_3_out);
  and and_6 (S5, A, not_2_out, C);
  and and_7 (S6, A, B, not_3_out);
  and and_8 (S7, A, B, C);
endmodule

module BASCULE_D_1__BIT (
  input  D,
  input  CLK,
  output out_3
);

  wire nand_1_out, nand_2_out, nand_4_out, not_1_out;

  not not_1 (not_1_out, D);
  nand nand_1 (nand_1_out, D, CLK);
  nand nand_2 (nand_2_out, CLK, not_1_out);
  nand nand_3 (out_3, nand_1_out, nand_4_out);
  nand nand_4 (nand_4_out, out_3, nand_2_out);
endmodule

module REGISTRE_4_BIT (
  input  [3:0] BUS_R,
  input  WA,
  input  CK,
  input  RA1,
  input  RA2,
  output [3:0] BUS_Y,
  output [3:0] BUS_X
);

  wire controlled_buffer_1_out, controlled_buffer_2_out, controlled_buffer_3_out, controlled_buffer_4_out,
       d_ff_1_q, d_ff_2_q, d_ff_3_q, d_ff_4_q;

  assign controlled_buffer_1_out = WA ? BUS_R[2] : 1'bz;  // Controlled_Buffer controlled_buffer_1
  assign controlled_buffer_2_out = WA ? BUS_R[3] : 1'bz;  // Controlled_Buffer controlled_buffer_2
  assign controlled_buffer_3_out = WA ? BUS_R[0] : 1'bz;  // Controlled_Buffer controlled_buffer_3
  assign controlled_buffer_4_out = WA ? BUS_R[1] : 1'bz;  // Controlled_Buffer controlled_buffer_4
  D_Flip_Flop d_ff_1 (.clk(CK), .D(controlled_buffer_3_out), .Q(d_ff_1_q));  // open: Qn, preset, en, reset
  D_Flip_Flop d_ff_2 (.clk(CK), .D(controlled_buffer_4_out), .Q(d_ff_2_q));  // open: Qn, preset, en, reset
  D_Flip_Flop d_ff_3 (.clk(CK), .D(controlled_buffer_1_out), .Q(d_ff_3_q));  // open: Qn, preset, en, reset
  D_Flip_Flop d_ff_4 (.clk(CK), .D(controlled_buffer_2_out), .Q(d_ff_4_q));  // open: Qn, preset, en, reset
  assign BUS_X[0] = RA1 ? d_ff_1_q : 1'bz;  // Controlled_Buffer controlled_buffer_5
  assign BUS_X[1] = RA1 ? d_ff_2_q : 1'bz;  // Controlled_Buffer controlled_buffer_6
  assign BUS_X[2] = RA1 ? d_ff_3_q : 1'bz;  // Controlled_Buffer controlled_buffer_7
  assign BUS_Y[0] = RA2 ? d_ff_1_q : 1'bz;  // Controlled_Buffer controlled_buffer_8
  assign BUS_X[3] = RA1 ? d_ff_4_q : 1'bz;  // Controlled_Buffer controlled_buffer_9
  assign BUS_Y[1] = RA2 ? d_ff_2_q : 1'bz;  // Controlled_Buffer controlled_buffer_10
  assign BUS_Y[2] = RA2 ? d_ff_3_q : 1'bz;  // Controlled_Buffer controlled_buffer_11
  assign BUS_Y[3] = RA2 ? d_ff_4_q : 1'bz;  // Controlled_Buffer controlled_buffer_12
endmodule

module BANC_DE_REGISTRE (
  input  [3:0] BUS_R,
  input  [3:0] WA,
  input  CLK,
  input  [3:0] RA1,
  input  [3:0] RA2,
  output [3:0] out_6,
  output [3:0] out_7
);

  REGISTRE_4_BIT registre_4_bit_1 (
    .BUS_R(BUS_R), .BUS_Y(out_6), .BUS_X(out_7), .WA(WA[0]), .CK(CLK), .RA1(RA1[0]), .RA2(RA2[0]));
  REGISTRE_4_BIT registre_4_bit_2 (
    .BUS_R(BUS_R), .BUS_Y(out_6), .BUS_X(out_7), .WA(WA[1]), .CK(CLK), .RA1(RA1[1]), .RA2(RA2[1]));
  REGISTRE_4_BIT registre_4_bit_3 (
    .BUS_R(BUS_R), .BUS_Y(out_6), .BUS_X(out_7), .WA(WA[2]), .CK(CLK), .RA1(RA1[2]), .RA2(RA2[2]));
  REGISTRE_4_BIT registre_4_bit_4 (
    .BUS_R(BUS_R), .BUS_Y(out_6), .BUS_X(out_7), .WA(WA[3]), .CK(CLK), .RA1(RA1[3]), .RA2(RA2[3]));
endmodule

module REGISTRE_D_INSTRUCTIONS (
  input  [11:0] in_1,
  input  in_2,
  input  in_3,
  input  in_4,
  output [11:0] out_5
);

  REGISTRE_4_BIT registre_4_bit_1 (
    .BUS_R(in_1[11:8]), .BUS_X(out_5[11:8]), .WA(in_2), .CK(in_3), .RA1(in_4));  // open: BUS_Y, RA2
  REGISTRE_4_BIT registre_4_bit_2 (
    .BUS_R(in_1[3:0]), .BUS_X(out_5[3:0]), .WA(in_2), .CK(in_3), .RA1(in_4));  // open: BUS_Y, RA2
  REGISTRE_4_BIT registre_4_bit_3 (
    .BUS_R(in_1[7:4]), .BUS_X(out_5[7:4]), .WA(in_2), .CK(in_3), .RA1(in_4));  // open: BUS_Y, RA2
endmodule

module LIASION_ALU____BANC_DE_REGISTRE (
  input  [3:0] in_1,
  input  [3:0] in_2,
  input  in_3,
  input  [2:0] in_4,
  input  [3:0] in_5,
  input  [3:0] in_6,
  output [3:0] out_7,
  output out_8
);

  wire [3:0] banc_de_registre_1_out_6, banc_de_registre_1_out_7;

  BANC_DE_REGISTRE banc_de_registre_1 (
    .BUS_R(in_1), .WA(in_2), .CLK(in_3), .RA1(in_5), .RA2(in_6), .out_6(banc_de_registre_1_out_6),
    .out_7(banc_de_registre_1_out_7));
  Hex_Digit_Display hex_digit_display_1 (.value(banc_de_registre_1_out_6));  // open: dp
  Hex_Digit_Display hex_digit_display_2 (.value(banc_de_registre_1_out_7));  // open: dp
  Hex_Digit_Display hex_digit_display_3 (.value(out_7));  // open: dp
  ALU_4__BIT alu_4_bit_1 (
    .in_1(banc_de_registre_1_out_6), .in_2(banc_de_registre_1_out_7), .in_3(in_4), .out_4(out_8),
    .out_5(out_7));

  // Notes on the sheet:
  //   00 : OU |  01 : ET | 10 NOT | 11 ADD  
endmodule

module REGISTRE_ADRESSES_DE_DONNEES (
  input  [3:0] in_1,
  input  [3:0] in_2,
  input  in_3,
  input  in_4,
  input  in_5,
  input  in_6
);

  REGISTRE_4_BIT registre_4_bit_1 (.BUS_R(in_2), .BUS_X(in_1), .WA(in_3), .CK(in_5), .RA1(in_6));  // open: BUS_Y, RA2
  REGISTRE_4_BIT registre_4_bit_2 (.BUS_R(in_2), .BUS_X(in_1), .WA(in_4), .CK(in_5), .RA1(in_6));  // open: BUS_Y, RA2

  // Notes on the sheet:
  //   AD
  //   PC
endmodule

module UNITE_DE_CONTROLE (
  input  [11:0] in_1,
  input  in_2,
  input  in_3,
  input  in_4,
  output [2:0] out_5,
  output [3:0] out_6,
  output [3:0] out_7,
  output [3:0] out_8
);

  wire [11:3] registre_d_instructions_1_out_5;

  REGISTRE_D_INSTRUCTIONS registre_d_instructions_1 (
    .in_1(in_1), .in_2(in_2), .in_3(in_3), .out_5({registre_d_instructions_1_out_5, out_5}), .in_4(in_4));
  Decoder #(.select(2), .enable("false")) decoder_1 (
    .out0(out_6[0]), .out1(out_6[1]), .out2(out_6[2]), .out3(out_6[3]),
    .sel(registre_d_instructions_1_out_5[4:3]));
  Decoder #(.select(2), .enable("false")) decoder_2 (
    .out0(out_7[0]), .out1(out_7[1]), .out2(out_7[2]), .out3(out_7[3]),
    .sel(registre_d_instructions_1_out_5[6:5]));
  Decoder #(.select(2), .enable("false")) decoder_3 (
    .out0(out_8[0]), .out1(out_8[1]), .out2(out_8[2]), .out3(out_8[3]),
    .sel(registre_d_instructions_1_out_5[8:7]));
endmodule
